// Logisim project teste.circ as structural Verilog
module main (
  input  A,
  input  B,
  output S1,
  output S2,
  output S3,
  output S4,
  output S5
);

  and and_1 (S1, A, B);
  or or_1 (S2, A, B);
  not not_1 (S3, B);
  not not_2 (S4, A);
  AULA1 aula1_1 (.A(A), .B(B), .Y(S5));
endmodule

// VHDL entity AULA1, as the project stores it:
LIBRARY ieee;
USE ieee.std_logic_1164.all;

ENTITY AULA1 IS
  PORT (
  	A : in STD_LOGIC;
  	B : in STD_LOGIC;
  	Y : out STD_LOGIC
    );
END AULA1;


ARCHITECTURE Behavioral OF AULA1 IS

BEGIN


	Y <= A AND B;
END Behavioral;
