// Logisim project edsonbaitola.circ as structural Verilog
module a (
  input  in_1,
  input  in_2,
  input  in_3,
  output out_4
);

  VHDL vhdl_1 (.x(in_1), .y(in_2), .z(in_3), .sum_out(out_4));  // open: carry_out
endmodule

// VHDL entity VHDL, as the project stores it:
library ieee;
use ieee.std_logic_1164.all;

entity VHDL is

	port(
	x : in STD_LOGIC ;
	y : in STD_LOGIC ;
	z : in STD_LOGIC ;
	sum_out : out STD_LOGIC;
	carry_out : out STD_LOGIC
	
	
	);
	
end VHDL;

architecture Comportamental  of VHDL is

	begin
		sum_out <= (x XOR y) XOR z;
		carry_out <= (x AND y) OR (z AND(x XOR y));

end Comportamental;
